# Fritzing sketch fritzing_sketch (saved by Fritzing 0.9.4)
breadboards: 1

parts:
  LED1 = LED - 5mm [color="Green (555nm)" package="5 mm [THT]"]
  R1 = Resistor [tolerance=±5% resistance=220 package=THT]
  C1 = Electrolytic Capacitor [capacitance=1µF package="100 mil [THT, electrolytic]"]
  R5 = Resistor [tolerance=±5% resistance=220 package=THT]
  U1 = 555 Timer [package="DIP8 [THT]"]
  C2 = Electrolytic Capacitor [capacitance=1µF package="100 mil [THT, electrolytic]"]
  R6 = Resistor [tolerance=±5% resistance=220 package=THT]
  LED2 = LED - 5mm [color="Red (633nm)" package="5 mm [THT]"]
  C3 = Ceramic Capacitor [capacitance=100nF package="100 mil [THT, multilayer]"]
  R8 = Resistor [tolerance=±5% resistance=220 package=THT]
  R9 = Resistor [tolerance=±5% resistance=220 package=THT]
  R10 = Resistor [tolerance=±5% resistance=220 package=THT]
  Part1 = NE555 Astable Breadboard Adapter

nets:
  GND1: LED1.cathode, C1.-, U1.Ground, C2.-, LED2.cathode, Part1.GND1, Part1.GND2, Part1.GND3
  N1: LED1.anode, R1.Pin_0
  N2: R1.Pin_1, Part1.OUT1, Part1.OUT2, Part1.OUT3
  N3: C1.+, R5.Pin_1, Part1.TRI1, Part1.TRI2, Part1.TRI3
  N4: R5.Pin_0, R10.Pin_0, Part1.DIS1, Part1.DIS2, Part1.DIS3
  N5: U1.Trigger, U1.Threshold, C2.+, R9.Pin_0
  N6: U1.Output, R6.Pin_1
  N7: U1.Reset, R10.Pin_1, Part1.VCC1
  N8: U1.Control_Voltage, C3.1
  N9: U1.Discharge, R8.Pin_1, R9.Pin_1
  N10: U1.Vcc_Supply_Voltage, R8.Pin_0
  N11: R6.Pin_0, LED2.anode
